// Digital circuit Simplic-Refactor.dig as structural Verilog
module Simplic_Refactor (
  input  CLK,
  input  CLK_2
);

  wire add_4_c_o, add_7_c_o, add_8_c_o, and_1_out, and_2_out, and_3_out, and_5_out, and_6_out, and_7_out,
       and_8_out, and_10_out, and_11_out, and_12_out, and_13_out, and_14_out, and_15_out, and_16_out,
       and_20_out, C_2_q, C_4_q, C_5_q, C_q, comparator_1_eq, multiplexer_1_out, multiplexer_7_out,
       multiplexer_8_out, N_2_q, N_4_q, N_5_q, N_q, nor_1_out, or_3_out, or_4_out, or_5_out, or_6_out,
       or_7_out, or_8_out, or_9_out, or_10_out, SEL_2_q, sub_1_c_o, sub_4_c_o, sub_5_c_o, undriven_48,
       undriven_49, undriven_50, undriven_51, undriven_81, undriven_82, undriven_89, undriven_90,
       undriven_91, undriven_93, undriven_94, undriven_95, undriven_96, undriven_97, undriven_98,
       undriven_105, undriven_106, undriven_107, undriven_108, V_2_q, V_4_q, V_5_q, V_q, xnor_1_out,
       xnor_2_out, xnor_3_out, xnor_4_out, xnor_5_out, xnor_6_out, xor_1_out, xor_2_out, xor_3_out,
       xor_4_out, xor_5_out, xor_6_out, xor_9_out, Z_2_q, Z_4_q, Z_5_q, Z_q;
  wire [0:0] demultiplexer_7_out_0;
  wire [1:0] and_4_out, and_9_out, or_1_out, or_1_out_2, or_2_out, sub_3_c_o, undriven_109;
  wire [2:0] INSTR_2_d_2, INSTR_d_2;
  wire [3:0] C_3_q, not_1_out, not_2_out, undriven_111;
  wire [4:0] driver_17_out;
  wire [7:0] and_22_out, and_22_out_2, decoder_1_out_7, decoder_1_out_15, decoder_2_out_7, decoder_2_out_15,
       decoder_3_out_7, decoder_3_out_15, or_15_out, or_15_out_2;
  wire [11:0] INSTR_2_d, INSTR_d;
  wire [15:0] add_1_s, add_2_s, add_3_s, add_4_s, add_5_s, add_6_s, add_7_s, add_8_s, Addr_2_q, Addr_3_q,
       Addr_4_q, Addr_5_q, Addr_6_q, Addr_7_q, Addr_8_q, Addr_9_q, Addr_q, and_18_out, and_19_out,
       and_21_out, and_23_out, and_24_out, ASR_2_out, ASR_out, bitextender_1_out, bitextender_2_out, BUF_2_q,
       BUF_3_q, BUF_4_q, BUF_5_q, BUF_6_q, BUF_7_q, BUF_8_q, BUF_9_q, BUF_q, demultiplexer_1_out_0,
       demultiplexer_1_out_1, demultiplexer_1_out_2, demultiplexer_1_out_3, demultiplexer_1_out_4,
       demultiplexer_1_out_5, demultiplexer_1_out_6, demultiplexer_1_out_7, demultiplexer_1_out_8,
       demultiplexer_1_out_9, demultiplexer_1_out_10, demultiplexer_1_out_11, demultiplexer_1_out_12,
       demultiplexer_1_out_13, demultiplexer_1_out_14, demultiplexer_1_out_15, demultiplexer_2_out_0,
       demultiplexer_2_out_1, demultiplexer_2_out_2, demultiplexer_2_out_3, demultiplexer_2_out_4,
       demultiplexer_2_out_5, demultiplexer_2_out_6, demultiplexer_2_out_7, demultiplexer_2_out_8,
       demultiplexer_2_out_9, demultiplexer_2_out_10, demultiplexer_2_out_11, demultiplexer_2_out_12,
       demultiplexer_2_out_13, demultiplexer_2_out_14, demultiplexer_2_out_15, demultiplexer_3_out_0,
       demultiplexer_3_out_1, demultiplexer_3_out_2, demultiplexer_3_out_3, demultiplexer_3_out_4,
       demultiplexer_3_out_5, demultiplexer_3_out_6, demultiplexer_3_out_7, demultiplexer_3_out_8,
       demultiplexer_3_out_9, demultiplexer_3_out_10, demultiplexer_3_out_11, demultiplexer_3_out_12,
       demultiplexer_3_out_13, demultiplexer_3_out_14, demultiplexer_3_out_15, demultiplexer_4_out_0,
       demultiplexer_4_out_1, demultiplexer_4_out_2, demultiplexer_4_out_3, demultiplexer_4_out_4,
       demultiplexer_4_out_5, demultiplexer_4_out_6, demultiplexer_4_out_7, demultiplexer_4_out_8,
       demultiplexer_4_out_9, demultiplexer_4_out_10, demultiplexer_4_out_11, demultiplexer_4_out_12,
       demultiplexer_4_out_13, demultiplexer_4_out_14, demultiplexer_4_out_15, demultiplexer_5_out_0,
       demultiplexer_5_out_1, demultiplexer_5_out_2, demultiplexer_5_out_3, demultiplexer_5_out_4,
       demultiplexer_5_out_5, demultiplexer_5_out_6, demultiplexer_5_out_7, demultiplexer_5_out_8,
       demultiplexer_5_out_9, demultiplexer_5_out_10, demultiplexer_5_out_11, demultiplexer_5_out_12,
       demultiplexer_5_out_13, demultiplexer_5_out_14, demultiplexer_5_out_15, demultiplexer_6_out_0,
       demultiplexer_6_out_1, demultiplexer_6_out_2, demultiplexer_6_out_3, demultiplexer_6_out_4,
       demultiplexer_6_out_5, demultiplexer_6_out_6, demultiplexer_6_out_7, demultiplexer_6_out_8,
       demultiplexer_6_out_9, demultiplexer_6_out_10, demultiplexer_6_out_11, demultiplexer_6_out_12,
       demultiplexer_6_out_13, demultiplexer_6_out_14, demultiplexer_6_out_15, demultiplexer_7_out_1,
       demultiplexer_7_out_2, demultiplexer_7_out_3, demultiplexer_7_out_5, demultiplexer_7_out_6,
       demultiplexer_7_out_7, demultiplexer_7_out_9, demultiplexer_7_out_10, demultiplexer_7_out_11,
       demultiplexer_7_out_13, demultiplexer_7_out_14, demultiplexer_7_out_15, demultiplexer_8_out_0,
       demultiplexer_8_out_1, demultiplexer_8_out_2, demultiplexer_8_out_3, demultiplexer_8_out_4,
       demultiplexer_8_out_5, demultiplexer_8_out_6, demultiplexer_8_out_7, demultiplexer_8_out_8,
       demultiplexer_8_out_9, demultiplexer_8_out_10, demultiplexer_8_out_11, demultiplexer_8_out_12,
       demultiplexer_8_out_13, demultiplexer_8_out_14, demultiplexer_8_out_15, demultiplexer_9_out_0,
       demultiplexer_9_out_1, demultiplexer_9_out_2, demultiplexer_9_out_3, demultiplexer_9_out_4,
       demultiplexer_9_out_5, demultiplexer_9_out_6, demultiplexer_9_out_7, demultiplexer_9_out_8,
       demultiplexer_9_out_9, demultiplexer_9_out_10, demultiplexer_9_out_11, demultiplexer_9_out_12,
       demultiplexer_9_out_13, demultiplexer_9_out_14, demultiplexer_9_out_15, div_1_q, div_1_r, div_2_q,
       div_2_r, div_3_q, div_3_r, div_4_q, div_4_r, div_5_q, div_5_r, driver_1_out, driver_9_out, Link_2_q,
       Link_3_q, Link_4_q, Link_5_q, Link_6_q, Link_7_q, Link_8_q, Link_9_q, Link_q, LSL_2_out, LSL_3_out,
       LSL_out, LSR_2_out, LSR_out, MEM_2_d, MEM_d, mul_1_mul, mul_1_mul_2, mul_2_mul, mul_2_mul_2,
       mul_3_mul, mul_3_mul_2, mul_4_mul, mul_4_mul_2, mul_5_mul, mul_5_mul_2, multiplexer_3_out,
       multiplexer_4_out, multiplexer_5_out, multiplexer_9_out, multiplexer_11_out, multiplexer_12_out,
       multiplexer_13_out, multiplexer_14_out, multiplexer_15_out, multiplexer_16_out, multiplexer_17_out,
       multiplexer_18_out, multiplexer_19_out, multiplexer_20_out, multiplexer_21_out, multiplexer_22_out,
       multiplexer_23_out, multiplexer_24_out, multiplexer_26_out, multiplexer_27_out, multiplexer_28_out,
       multiplexer_29_out, multiplexer_30_out, multiplexer_31_out, multiplexer_32_out, multiplexer_33_out,
       multiplexer_36_out, multiplexer_37_out, multiplexer_39_out, multiplexer_40_out, multiplexer_41_out,
       multiplexer_42_out, multiplexer_43_out, multiplexer_44_out, multiplexer_45_out, multiplexer_46_out,
       multiplexer_48_out, multiplexer_49_out, multiplexer_50_out, nor_2_out, nor_3_out, nor_4_out,
       nor_5_out, nor_6_out, or_11_out, or_12_out, or_13_out, or_14_out, or_16_out, or_17_out, PC_2_out,
       PC_3_out, PC_4_out, PC_5_out, PC_6_out, PC_7_out, PC_8_out, PC_9_out, PC_10_out, PC_out, R1_q, R2_q,
       R3_q, R4_q, R5_q, R6_q, R7_q, R8_q, R9_q, R91_q, R92_q, R93_q, R94_q, R95_q, R96_q, R97_q, R98_q,
       R99_q, R109_q, R110_q, R111_q, R112_q, R113_q, R114_q, R115_q, R116_q, R117_q, R118_q, R119_q, R120_q,
       R121_q, R122_q, R123_q, R124_q, R125_q, R126_q, R127_q, R128_q, R129_q, R130_q, R131_q, R132_q,
       R133_q, R134_q, R135_q, R136_q, R137_q, R138_q, R139_q, R140_q, R141_q, R142_q, R143_q, R144_q,
       R145_q, R146_q, R147_q, R148_q, R149_q, R150_q, R151_q, R152_q, R153_q, R154_q, R155_q, R156_q,
       R157_q, R158_q, R159_q, R160_q, R161_q, R162_q, R163_q, R164_q, R165_q, R166_q, R167_q, R168_q,
       R169_q, R170_q, R171_q, RET_2_q, RET_3_q, RET_4_q, RET_5_q, RET_6_q, RET_7_q, RET_8_q, RET_9_q, RET_q,
       ROR_2_out, ROR_out, STA_2_q, STA_3_q, STA_4_q, STA_5_q, STA_6_q, STA_7_q, STA_8_q, STA_9_q, STA_q,
       sub_1_s, sub_2_s, sub_3_s, sub_4_s, sub_5_s, t29_q, t31_q, t33_q, t35_q, t36_q, t37_q, t38_q, t39_q,
       t40_q, t41_q, t42_q, undriven, undriven_2, undriven_3, undriven_4, undriven_5, undriven_6, undriven_7,
       undriven_8, undriven_9, undriven_10, undriven_11, undriven_12, undriven_13, undriven_14, undriven_15,
       undriven_16, undriven_33, undriven_34, undriven_35, undriven_36, undriven_37, undriven_38,
       undriven_39, undriven_40, undriven_41, undriven_42, undriven_43, undriven_44, undriven_45,
       undriven_46, undriven_47, undriven_52, undriven_53, undriven_54, undriven_55, undriven_56,
       undriven_57, undriven_58, undriven_59, undriven_60, undriven_61, undriven_62, undriven_63,
       undriven_79, undriven_80, undriven_83, undriven_84, undriven_85, undriven_86, undriven_87,
       undriven_88, undriven_92, undriven_99, undriven_100, undriven_101, undriven_102, undriven_103,
       undriven_104, undriven_110, undriven_112, undriven_113, undriven_114, xor_7_out, xor_8_out,
       xor_10_out, xor_11_out, xor_12_out;
  wire [15:1] demultiplexer_7_out_0_2, demultiplexer_7_out_4, demultiplexer_7_out_8, demultiplexer_7_out_12,
       t30_q, t32_q, t34_q, undriven_17, undriven_18, undriven_19, undriven_20, undriven_21, undriven_22,
       undriven_23, undriven_24, undriven_25, undriven_26, undriven_27, undriven_28, undriven_29,
       undriven_30, undriven_31, undriven_32;
  wire [15:5] driver_17_out_2;
  wire [16:0] undriven_78;
  wire [16:16] undriven_64, undriven_65, undriven_66, undriven_67, undriven_68, undriven_69, undriven_70,
       undriven_71, undriven_72, undriven_73, undriven_74, undriven_75, undriven_76, undriven_77;

  ROM #(.bigEndian("true"), .AddrBits(16), .Bits(16)) INSTR (
    .A(PC_4_out), .sel(1'b1), .D({and_4_out[1], INSTR_d_2, INSTR_d}));
  EEPROMDualPort #(.AddrBits(16), .Bits(16)) MEM (
    .A(driver_9_out), .Din(driver_1_out), .str(and_1_out), .C(CLK), .ld(1'b1), .D(MEM_d));
  ROM #(.bigEndian("true"), .AddrBits(16), .Bits(16)) INSTR_2 (
    .A(undriven_114), .sel(1'b1), .D({and_9_out[1], INSTR_2_d_2, INSTR_2_d}));
  EEPROMDualPort #(.AddrBits(16), .Bits(16)) MEM_2 (
    .A(undriven_113), .Din(undriven_112), .str(and_7_out), .C(CLK_2), .ld(1'b1), .D(MEM_2_d));
  assign {or_1_out_2, or_1_out} = INSTR_d[3:0] | INSTR_d[7:4] | INSTR_d[11:8];  // Or or_1, 4 bits wide
  and and_1 (and_1_out, INSTR_d_2[0], INSTR_d_2[1], ~INSTR_d_2[2], ~and_4_out[1]);  // And
  and and_2 (and_2_out, INSTR_d_2[1], ~INSTR_d_2[2], ~and_4_out[1]);  // And
  and and_3 (and_3_out, INSTR_d_2[1], INSTR_d_2[2]);
  and and_4 (and_4_out[0], INSTR_d_2[0], ~and_4_out[1]);  // And
  and and_5 (and_5_out, INSTR_d_2[0], INSTR_d_2[1], INSTR_d_2[2], and_4_out[1]);
  and and_6 (and_6_out, ~and_4_out[1], INSTR_d_2[2], INSTR_d_2[1], INSTR_d_2[0]);  // And
  assign or_2_out = or_1_out | or_1_out_2;  // Or or_2, 2 bits wide
  or or_3 (or_3_out, and_3_out, and_4_out[1]);
  and and_7 (and_7_out, INSTR_2_d_2[0], INSTR_2_d_2[1], ~INSTR_2_d_2[2], ~and_9_out[1]);  // And
  and and_8 (and_8_out, INSTR_2_d_2[1], INSTR_2_d_2[2]);
  and and_9 (and_9_out[0], INSTR_2_d_2[0], ~and_9_out[1]);  // And
  and and_10 (and_10_out, nor_1_out, and_5_out);
  and and_11 (and_11_out, nor_1_out, and_6_out);
  nor nor_1 (nor_1_out, or_2_out[0], or_2_out[1]);
  or or_4 (or_4_out, and_8_out, and_9_out[1]);
  or or_5 (or_5_out, C_3_q[3], C_3_q[2]);
  or or_6 (or_6_out, ~C_3_q[3], C_3_q[2]);  // Or
  xor xor_1 (xor_1_out, C_3_q[3], C_3_q[0]);
  and and_12 (and_12_out, ~C_3_q[2], xnor_1_out);  // And
  or or_7 (or_7_out, C_3_q[2], ~xnor_1_out);  // Or
  xnor xnor_1 (xnor_1_out, C_3_q[3], C_3_q[0]);
  and and_13 (and_13_out, ~C_3_q[1], ~C_3_q[0]);  // And
  assign not_1_out = ~C_3_q;  // Not not_1, 4 bits wide
  Multiplexer #(.Selector_Bits(4)) multiplexer_1 (
    .sel(INSTR_d[3:0]), .in_0(C_3_q[0]), .in_1(not_1_out[0]), .in_2(C_3_q[1]), .in_3(not_1_out[1]),
    .in_4(C_3_q[2]), .in_5(not_1_out[2]), .in_6(C_3_q[3]), .in_7(not_1_out[3]), .in_8(or_5_out),
    .in_9(or_6_out), .in_10(xor_1_out), .in_11(and_12_out), .in_12(or_7_out), .in_13(xnor_1_out),
    .in_14(and_13_out), .in_15(1'b1), .out(multiplexer_1_out));
  assign not_2_out = ~undriven_111;  // Not not_2, 4 bits wide
  or or_8 (or_8_out, undriven_111[3], undriven_111[2]);
  or or_9 (or_9_out, ~undriven_111[3], undriven_111[2]);  // Or
  xor xor_2 (xor_2_out, undriven_111[3], undriven_111[0]);
  and and_14 (and_14_out, ~undriven_111[2], xnor_2_out);  // And
  or or_10 (or_10_out, undriven_111[2], ~xnor_2_out);  // Or
  xnor xnor_2 (xnor_2_out, undriven_111[3], undriven_111[0]);
  and and_15 (and_15_out, ~undriven_111[1], ~undriven_111[0]);  // And
  Add #(.Bits(16)) add_1 (.a(driver_1_out), .b(16'h1), .c_i(1'b0), .s(add_1_s));  // open: c_o
  Add #(.Bits(16)) add_2 (.a(driver_1_out), .b(driver_9_out), .c_i(1'b0), .s(add_2_s));  // open: c_o
  BitExtender #(.inputBits(4)) bitextender_1 (.in(INSTR_d[3:0]), .out(bitextender_1_out));
  Multiplexer #(.Selector_Bits(4)) multiplexer_2 (
    .in_0(undriven_111[0]), .in_1(not_2_out[0]), .in_2(undriven_111[1]), .in_3(not_2_out[1]),
    .in_4(undriven_111[2]), .in_5(not_2_out[2]), .in_6(undriven_111[3]), .in_7(not_2_out[3]),
    .in_8(or_8_out), .in_9(or_9_out), .in_10(xor_2_out), .in_11(and_14_out), .in_12(or_10_out),
    .in_13(xnor_2_out), .in_14(and_15_out), .in_15(1'b1));  // open: sel, out
  Multiplexer #(.Bits(16)) multiplexer_3 (
    .sel(multiplexer_1_out), .in_0(add_1_s), .in_1(driver_9_out), .out(multiplexer_3_out));
  Multiplexer #(.Bits(16)) multiplexer_4 (
    .sel(multiplexer_1_out), .in_0(add_1_s), .in_1(add_2_s), .out(multiplexer_4_out));
  Add #(.Bits(16)) add_3 (.a(driver_9_out), .b(bitextender_1_out), .c_i(1'b0), .s(add_3_s));  // open: c_o
  BarrelShifter #(.Bits(16)) LSL (.in(driver_1_out), .shift(5'b01000), .out(LSL_out));
  assign or_11_out = {{8{1'b0}}, INSTR_d[7:0]} | LSL_out;  // Or or_11, 16 bits wide
  BarrelShifter #(.Bits(16)) LSL_2 (.in(driver_1_out), .shift(driver_17_out), .out(LSL_2_out));
  BarrelShifter #(.Bits(16), .direction("right")) LSR (.in(driver_1_out), .shift(driver_17_out), .out(LSR_out));
  BarrelShifter #(.Bits(16), .barrelShifterMode("arithmetic"), .direction("right")) ASR (
    .in(driver_1_out), .shift(driver_17_out), .out(ASR_out));
  BarrelShifter #(.Bits(16), .barrelShifterMode("rotate"), .direction("right")) ROR (
    .in(driver_1_out), .shift(driver_17_out), .out(ROR_out));
  BarrelShifter #(.Bits(16)) LSL_3 (.in(undriven_110), .shift(undriven_108), .out(LSL_3_out));
  BarrelShifter #(.Bits(16), .direction("right")) LSR_2 (.in(undriven_110), .shift(undriven_108), .out(LSR_2_out));
  BarrelShifter #(.Bits(16), .barrelShifterMode("arithmetic"), .direction("right")) ASR_2 (
    .in(undriven_110), .shift(undriven_108), .out(ASR_2_out));
  BarrelShifter #(.Bits(16), .barrelShifterMode("rotate"), .direction("right")) ROR_2 (
    .in(undriven_110), .shift(undriven_108), .out(ROR_2_out));
  Multiplexer #(.Selector_Bits(2), .Bits(16)) multiplexer_5 (
    .sel(INSTR_d[5:4]), .in_0(LSL_2_out), .in_1(LSR_out), .in_2(ASR_out), .in_3(ROR_out),
    .out(multiplexer_5_out));
  Multiplexer #(.Selector_Bits(2), .Bits(16)) multiplexer_6 (
    .sel(undriven_109), .in_0(LSL_3_out), .in_1(LSR_2_out), .in_2(ASR_2_out), .in_3(ROR_2_out));  // open: out
  BitSelector #(.Selector_Bits(4)) bitselector_1 (.in(undriven_107));  // open: sel, out
  BitSelector #(.Selector_Bits(4)) bitselector_2 (.in(undriven_106));  // open: sel, out
  BitSelector #(.Selector_Bits(4)) bitselector_3 (.in(undriven_105));  // open: sel, out
  Comparator #(.Bits(16)) comparator_1 (.a(multiplexer_14_out), .b({16{1'b0}}), .eq(comparator_1_eq));  // open: gt, lt
  Register SEL ();  // open: D, C, en, Q
  xnor xnor_3 (xnor_3_out, undriven_93, undriven_94);
  xor xor_3 (xor_3_out, undriven_95, undriven_96);
  xnor xnor_4 (xnor_4_out, undriven_97, undriven_98);
  Register Z (.C(undriven_90), .en(undriven_91), .Q(Z_q));  // open: D
  Register N (.C(undriven_90), .en(undriven_91), .Q(N_q));  // open: D
  Register C (.C(undriven_90), .en(undriven_91), .Q(C_q));  // open: D
  Register V (.C(undriven_90), .en(undriven_91), .Q(V_q));  // open: D
  xnor xnor_5 (xnor_5_out, driver_9_out[15], driver_17_out_2[15]);
  xor xor_4 (xor_4_out, driver_9_out[15], driver_17_out_2[15]);
  xnor xnor_6 (xnor_6_out, driver_17_out_2[15], multiplexer_14_out[15]);
  xor xor_5 (xor_5_out, xnor_5_out, multiplexer_14_out[15]);
  and and_16 (and_16_out, xor_4_out, xnor_6_out);
  Comparator #(.Bits(16)) comparator_2 (.a(undriven_92), .b({16{1'b0}}));  // open: gt, eq, lt
  xor xor_6 (xor_6_out, xnor_3_out, undriven_89);
  // And and_17 has open pins: In_1=xor_3_out, In_2=xnor_4_out, out=open
  Multiplexer #(.Selector_Bits(2)) multiplexer_7 (
    .sel(and_4_out), .in_0(xor_5_out), .in_1(and_16_out), .in_2(1'b0), .in_3(1'b0), .out(multiplexer_7_out));
  Register Z_2 (.C(undriven_81), .en(undriven_82), .Q(Z_2_q));  // open: D
  Register N_2 (.C(undriven_81), .en(undriven_82), .Q(N_2_q));  // open: D
  Register C_2 (.C(undriven_81), .en(undriven_82), .Q(C_2_q));  // open: D
  Register V_2 (.C(undriven_81), .en(undriven_82), .Q(V_2_q));  // open: D
  Add #(.Bits(16)) add_4 (.a(multiplexer_13_out), .b(multiplexer_11_out), .c_i(C_q), .s(add_4_s), .c_o(add_4_c_o));
  Sub #(.Bits(16)) sub_1 (.a(multiplexer_13_out), .b(multiplexer_11_out), .c_i(C_q), .s(sub_1_s), .c_o(sub_1_c_o));
  Mul #(.Bits(16)) mul_1 (.a(multiplexer_13_out), .b(multiplexer_11_out), .mul({mul_1_mul_2, mul_1_mul}));
  Div #(.Bits(16)) div_1 (.a(multiplexer_13_out), .b(multiplexer_11_out), .q(div_1_q), .r(div_1_r));
  assign and_18_out = multiplexer_13_out & multiplexer_11_out;  // And and_18, 16 bits wide
  assign or_12_out = multiplexer_13_out | multiplexer_11_out;  // Or or_12, 16 bits wide
  assign xor_7_out = multiplexer_13_out ^ multiplexer_11_out;  // XOr xor_7, 16 bits wide
  assign nor_2_out = ~(multiplexer_13_out | multiplexer_11_out);  // NOr nor_2, 16 bits wide
  Multiplexer #(.Selector_Bits(2)) multiplexer_8 (
    .sel(and_4_out), .in_0(sub_3_c_o[1]), .in_1(sub_3_c_o[0]), .in_2(1'b0), .in_3(1'b0),
    .out(multiplexer_8_out));
  Add #(.Bits(16)) add_5 (.a(undriven_80), .b(undriven_79), .c_i(C_2_q), .s(add_5_s));  // open: c_o
  Sub #(.Bits(16)) sub_2 (.a(undriven_80), .b(undriven_79), .c_i(C_2_q), .s(sub_2_s));  // open: c_o
  Mul #(.Bits(16)) mul_2 (.a(undriven_80), .b(undriven_79), .mul({mul_2_mul_2, mul_2_mul}));
  Div #(.Bits(16)) div_2 (.a(undriven_80), .b(undriven_79), .q(div_2_q), .r(div_2_r));
  assign and_19_out = undriven_80 & undriven_79;  // And and_19, 16 bits wide
  assign or_13_out = undriven_80 | undriven_79;  // Or or_13, 16 bits wide
  assign xor_8_out = undriven_80 ^ undriven_79;  // XOr xor_8, 16 bits wide
  assign nor_3_out = ~(undriven_80 | undriven_79);  // NOr nor_3, 16 bits wide
  Multiplexer #(.Selector_Bits(4), .Bits(16)) multiplexer_9 (
    .in_0(undriven_99), .in_1(undriven_100), .in_2(undriven_101), .in_3(undriven_102), .in_4(undriven_103),
    .in_5(undriven_104), .in_6(add_4_s), .in_7(sub_1_s), .in_8(mul_1_mul), .in_9(mul_1_mul_2),
    .in_10(div_1_q), .in_11(div_1_r), .in_12(and_18_out), .in_13(or_12_out), .in_14(xor_7_out),
    .in_15(nor_2_out), .out(multiplexer_9_out));  // open: sel
  xor xor_9 (xor_9_out, and_10_out, and_11_out);
  Register SEL_2 (.D(and_10_out), .C(CLK), .en(xor_9_out), .Q(SEL_2_q));
  and and_20 (and_20_out, SEL_2_q, or_3_out);
  Demultiplexer #(.Selector_Bits(4), .Bits(16)) demultiplexer_1 (
    .in(multiplexer_9_out), .out_0(demultiplexer_1_out_0), .out_1(demultiplexer_1_out_1),
    .out_2(demultiplexer_1_out_2), .out_3(demultiplexer_1_out_3), .out_4(demultiplexer_1_out_4),
    .out_5(demultiplexer_1_out_5), .out_6(demultiplexer_1_out_6), .out_7(demultiplexer_1_out_7),
    .out_8(demultiplexer_1_out_8), .out_9(demultiplexer_1_out_9), .out_10(demultiplexer_1_out_10),
    .out_11(demultiplexer_1_out_11), .out_12(demultiplexer_1_out_12), .out_13(demultiplexer_1_out_13),
    .out_14(demultiplexer_1_out_14), .out_15(demultiplexer_1_out_15));  // open: sel
  Register #(.Bits(16)) R155 (.D(demultiplexer_1_out_2), .C(undriven_90), .Q(R155_q));  // open: en
  Register #(.Bits(16)) R157 (.D(demultiplexer_1_out_4), .C(undriven_90), .Q(R157_q));  // open: en
  Register #(.Bits(16)) R159 (.D(demultiplexer_1_out_6), .C(undriven_90), .Q(R159_q));  // open: en
  Register #(.Bits(16)) R161 (.D(demultiplexer_1_out_8), .C(undriven_90), .Q(R161_q));  // open: en
  Register #(.Bits(16)) BUF (.D(demultiplexer_1_out_10), .C(undriven_90), .Q(BUF_q));  // open: en
  Register #(.Bits(16)) STA (.D(demultiplexer_1_out_12), .C(undriven_90), .Q(STA_q));  // open: en
  Register #(.Bits(16)) Link (.D(demultiplexer_1_out_14), .C(undriven_90), .Q(Link_q));  // open: en
  Register N_3 (.D(multiplexer_14_out[15]), .C(CLK), .en(and_20_out), .Q(C_3_q[3]));
  Register Z_3 (.D(comparator_1_eq), .C(CLK), .en(and_20_out), .Q(C_3_q[2]));
  Register C_3 (.D(multiplexer_8_out), .C(CLK), .en(and_20_out), .Q(C_3_q[1]));
  Register V_3 (.D(multiplexer_7_out), .C(CLK), .en(and_20_out), .Q(C_3_q[0]));
  Register #(.Bits(16)) R154 (.D(demultiplexer_1_out_1), .C(undriven_90), .Q(R154_q));  // open: en
  Register #(.Bits(16)) R156 (.D(demultiplexer_1_out_3), .C(undriven_90), .Q(R156_q));  // open: en
  Register #(.Bits(16)) R158 (.D(demultiplexer_1_out_5), .C(undriven_90), .Q(R158_q));  // open: en
  Register #(.Bits(16)) R160 (.D(demultiplexer_1_out_7), .C(undriven_90), .Q(R160_q));  // open: en
  Register #(.Bits(16)) R162 (.D(demultiplexer_1_out_9), .C(undriven_90), .Q(R162_q));  // open: en
  Register #(.Bits(16)) RET (.D(demultiplexer_1_out_11), .C(undriven_90), .Q(RET_q));  // open: en
  Register #(.Bits(16)) Addr (.D(demultiplexer_1_out_13), .C(undriven_90), .Q(Addr_q));  // open: en
  CounterPreset #(.Bits(16)) PC (
    .en(1'b1), .dir(1'b0), .in(demultiplexer_1_out_15), .clr(1'b0), .out(PC_out));  // open: C, ld, ovf
  Multiplexer #(.Selector_Bits(4), .Bits(16)) multiplexer_10 (
    .in_0(undriven_83), .in_1(undriven_84), .in_2(undriven_85), .in_3(undriven_86), .in_4(undriven_87),
    .in_5(undriven_88), .in_6(add_5_s), .in_7(sub_2_s), .in_8(mul_2_mul), .in_9(mul_2_mul_2),
    .in_10(div_2_q), .in_11(div_2_r), .in_12(and_19_out), .in_13(or_13_out), .in_14(xor_8_out),
    .in_15(nor_3_out), .out(undriven_78[15:0]));  // open: sel
  Demultiplexer #(.Selector_Bits(4), .Bits(16)) demultiplexer_2 (
    .in(undriven_78[15:0]), .out_0(demultiplexer_2_out_0), .out_1(demultiplexer_2_out_1),
    .out_2(demultiplexer_2_out_2), .out_3(demultiplexer_2_out_3), .out_4(demultiplexer_2_out_4),
    .out_5(demultiplexer_2_out_5), .out_6(demultiplexer_2_out_6), .out_7(demultiplexer_2_out_7),
    .out_8(demultiplexer_2_out_8), .out_9(demultiplexer_2_out_9), .out_10(demultiplexer_2_out_10),
    .out_11(demultiplexer_2_out_11), .out_12(demultiplexer_2_out_12), .out_13(demultiplexer_2_out_13),
    .out_14(demultiplexer_2_out_14), .out_15(demultiplexer_2_out_15));  // open: sel
  Add #(.Bits(16)) add_6 (
    .a(driver_9_out), .b({driver_17_out_2, driver_17_out}), .c_i(C_3_q[1]), .s(add_6_s), .c_o(sub_3_c_o[1]));
  Sub #(.Bits(16)) sub_3 (
    .a(driver_9_out), .b({driver_17_out_2, driver_17_out}), .c_i(C_3_q[1]), .s(sub_3_s), .c_o(sub_3_c_o[0]));
  Mul #(.Bits(16)) mul_3 (.a(driver_9_out), .b({driver_17_out_2, driver_17_out}), .mul({mul_3_mul_2, mul_3_mul}));
  Div #(.Bits(16)) div_3 (.a(driver_9_out), .b({driver_17_out_2, driver_17_out}), .q(div_3_q), .r(div_3_r));
  assign and_21_out = driver_9_out & {driver_17_out_2, driver_17_out};  // And and_21, 16 bits wide
  assign or_14_out = driver_9_out | {driver_17_out_2, driver_17_out};  // Or or_14, 16 bits wide
  assign xor_10_out = driver_9_out ^ {driver_17_out_2, driver_17_out};  // XOr xor_10, 16 bits wide
  assign nor_4_out = ~(driver_9_out | {driver_17_out_2, driver_17_out});  // NOr nor_4, 16 bits wide
  Multiplexer #(.Selector_Bits(4), .Bits(16)) multiplexer_11 (
    .in_0({16{1'b0}}), .in_1(R154_q), .in_2(R155_q), .in_3(R156_q), .in_4(R157_q), .in_5(R158_q),
    .in_6(R159_q), .in_7(R160_q), .in_8(R161_q), .in_9(R162_q), .in_10(BUF_q), .in_11(RET_q), .in_12(STA_q),
    .in_13(Addr_q), .in_14(Link_q), .in_15(PC_out), .out(multiplexer_11_out));  // open: sel
  Multiplexer #(.Selector_Bits(4), .Bits(16)) multiplexer_12 (
    .in_0({16{1'b0}}), .in_1(R154_q), .in_2(R155_q), .in_3(R156_q), .in_4(R157_q), .in_5(R158_q),
    .in_6(R159_q), .in_7(R160_q), .in_8(R161_q), .in_9(R162_q), .in_10(BUF_q), .in_11(RET_q), .in_12(STA_q),
    .in_13(Addr_q), .in_14(Link_q), .in_15(PC_out), .out(multiplexer_12_out));  // open: sel
  Multiplexer #(.Selector_Bits(4), .Bits(16)) multiplexer_13 (
    .in_0({16{1'b0}}), .in_1(R154_q), .in_2(R155_q), .in_3(R156_q), .in_4(R157_q), .in_5(R158_q),
    .in_6(R159_q), .in_7(R160_q), .in_8(R161_q), .in_9(R162_q), .in_10(BUF_q), .in_11(RET_q), .in_12(STA_q),
    .in_13(Addr_q), .in_14(Link_q), .in_15(PC_out), .out(multiplexer_13_out));  // open: sel
  Register #(.Bits(16)) R2 (.D(demultiplexer_2_out_2), .C(undriven_81), .en(undriven_76[16]), .Q(R2_q));
  Register #(.Bits(16)) R4 (.D(demultiplexer_2_out_4), .C(undriven_81), .en(undriven_74[16]), .Q(R4_q));
  Register #(.Bits(16)) R6 (.D(demultiplexer_2_out_6), .C(undriven_81), .en(undriven_72[16]), .Q(R6_q));
  Register #(.Bits(16)) R8 (.D(demultiplexer_2_out_8), .C(undriven_81), .en(undriven_70[16]), .Q(R8_q));
  Register #(.Bits(16)) BUF_2 (.D(demultiplexer_2_out_10), .C(undriven_81), .en(undriven_68[16]), .Q(BUF_2_q));
  Register #(.Bits(16)) STA_2 (.D(demultiplexer_2_out_12), .C(undriven_81), .en(undriven_66[16]), .Q(STA_2_q));
  Register #(.Bits(16)) Link_2 (.D(demultiplexer_2_out_14), .C(undriven_81), .en(undriven_64[16]), .Q(Link_2_q));
  BitExtender #(.inputBits(1)) bitextender_2 (.in(and_2_out), .out(bitextender_2_out));
  Register #(.Bits(16)) R1 (.D(demultiplexer_2_out_1), .C(undriven_81), .en(undriven_77[16]), .Q(R1_q));
  Register #(.Bits(16)) R3 (.D(demultiplexer_2_out_3), .C(undriven_81), .en(undriven_75[16]), .Q(R3_q));
  Register #(.Bits(16)) R5 (.D(demultiplexer_2_out_5), .C(undriven_81), .en(undriven_73[16]), .Q(R5_q));
  Register #(.Bits(16)) R7 (.D(demultiplexer_2_out_7), .C(undriven_81), .en(undriven_71[16]), .Q(R7_q));
  Register #(.Bits(16)) R9 (.D(demultiplexer_2_out_9), .C(undriven_81), .en(undriven_69[16]), .Q(R9_q));
  Register #(.Bits(16)) RET_2 (.D(demultiplexer_2_out_11), .C(undriven_81), .en(undriven_67[16]), .Q(RET_2_q));
  Register #(.Bits(16)) Addr_2 (.D(demultiplexer_2_out_13), .C(undriven_81), .en(undriven_65[16]), .Q(Addr_2_q));
  CounterPreset #(.Bits(16)) PC_2 (
    .en(1'b1), .C(undriven_81), .dir(1'b0), .in(demultiplexer_2_out_15), .out(PC_2_out));  // open: ld, clr, ovf
  Demultiplexer #(.Selector_Bits(4), .Bits(16)) demultiplexer_3 (
    .out_0(demultiplexer_3_out_0), .out_1(demultiplexer_3_out_1), .out_2(demultiplexer_3_out_2),
    .out_3(demultiplexer_3_out_3), .out_4(demultiplexer_3_out_4), .out_5(demultiplexer_3_out_5),
    .out_6(demultiplexer_3_out_6), .out_7(demultiplexer_3_out_7), .out_8(demultiplexer_3_out_8),
    .out_9(demultiplexer_3_out_9), .out_10(demultiplexer_3_out_10), .out_11(demultiplexer_3_out_11),
    .out_12(demultiplexer_3_out_12), .out_13(demultiplexer_3_out_13), .out_14(demultiplexer_3_out_14),
    .out_15(demultiplexer_3_out_15));  // open: sel, in
  Multiplexer #(.Selector_Bits(4), .Bits(16)) multiplexer_14 (
    .sel({and_4_out[1], INSTR_d_2}), .in_0(multiplexer_3_out), .in_1(multiplexer_4_out), .in_2(MEM_d),
    .in_3(driver_1_out), .in_4(or_11_out), .in_5(multiplexer_5_out), .in_6(add_6_s), .in_7(sub_3_s),
    .in_8(mul_3_mul), .in_9(mul_3_mul_2), .in_10(div_3_q), .in_11(div_3_r), .in_12(and_21_out),
    .in_13(or_14_out), .in_14(xor_10_out), .in_15(nor_4_out), .out(multiplexer_14_out));
  Decoder #(.Selector_Bits(4)) decoder_1 (
    .sel(INSTR_d[3:0]), .out_0(decoder_1_out_7[0]), .out_1(decoder_1_out_7[1]), .out_2(decoder_1_out_7[2]),
    .out_3(decoder_1_out_7[3]), .out_4(decoder_1_out_7[4]), .out_5(decoder_1_out_7[5]),
    .out_6(decoder_1_out_7[6]), .out_7(decoder_1_out_7[7]), .out_8(decoder_1_out_15[0]),
    .out_9(decoder_1_out_15[1]), .out_10(decoder_1_out_15[2]), .out_11(decoder_1_out_15[3]),
    .out_12(decoder_1_out_15[4]), .out_13(decoder_1_out_15[5]), .out_14(decoder_1_out_15[6]),
    .out_15(decoder_1_out_15[7]));
  Decoder #(.Selector_Bits(4)) decoder_2 (
    .sel(INSTR_d[7:4]), .out_0(decoder_2_out_7[0]), .out_1(decoder_2_out_7[1]), .out_2(decoder_2_out_7[2]),
    .out_3(decoder_2_out_7[3]), .out_4(decoder_2_out_7[4]), .out_5(decoder_2_out_7[5]),
    .out_6(decoder_2_out_7[6]), .out_7(decoder_2_out_7[7]), .out_8(decoder_2_out_15[0]),
    .out_9(decoder_2_out_15[1]), .out_10(decoder_2_out_15[2]), .out_11(decoder_2_out_15[3]),
    .out_12(decoder_2_out_15[4]), .out_13(decoder_2_out_15[5]), .out_14(decoder_2_out_15[6]),
    .out_15(decoder_2_out_15[7]));
  Decoder #(.Selector_Bits(4)) decoder_3 (
    .sel(INSTR_d[11:8]), .out_0(decoder_3_out_7[0]), .out_1(decoder_3_out_7[1]), .out_2(decoder_3_out_7[2]),
    .out_3(decoder_3_out_7[3]), .out_4(decoder_3_out_7[4]), .out_5(decoder_3_out_7[5]),
    .out_6(decoder_3_out_7[6]), .out_7(decoder_3_out_7[7]), .out_8(decoder_3_out_15[0]),
    .out_9(decoder_3_out_15[1]), .out_10(decoder_3_out_15[2]), .out_11(decoder_3_out_15[3]),
    .out_12(decoder_3_out_15[4]), .out_13(decoder_3_out_15[5]), .out_14(decoder_3_out_15[6]),
    .out_15(decoder_3_out_15[7]));
  assign {or_15_out_2, or_15_out} = {and_22_out_2, and_22_out} | {decoder_3_out_15, decoder_3_out_7};  // Or or_15, 16 bits wide
  assign {and_22_out_2, and_22_out} = bitextender_2_out & {decoder_2_out_15, decoder_2_out_7};  // And and_22, 16 bits wide
  Register #(.Bits(16)) R164 (.D(demultiplexer_3_out_2), .Q(R164_q));  // open: C, en
  Register #(.Bits(16)) R166 (.D(demultiplexer_3_out_4), .Q(R166_q));  // open: C, en
  Register #(.Bits(16)) R168 (.D(demultiplexer_3_out_6), .Q(R168_q));  // open: C, en
  Register #(.Bits(16)) R170 (.D(demultiplexer_3_out_8), .Q(R170_q));  // open: C, en
  Register #(.Bits(16)) BUF_3 (.D(demultiplexer_3_out_10), .Q(BUF_3_q));  // open: C, en
  Register #(.Bits(16)) STA_3 (.D(demultiplexer_3_out_12), .Q(STA_3_q));  // open: C, en
  Register #(.Bits(16)) Link_3 (.D(demultiplexer_3_out_14), .Q(Link_3_q));  // open: C, en
  Register #(.Bits(16)) R163 (.D(demultiplexer_3_out_1), .Q(R163_q));  // open: C, en
  Register #(.Bits(16)) R165 (.D(demultiplexer_3_out_3), .Q(R165_q));  // open: C, en
  Register #(.Bits(16)) R167 (.D(demultiplexer_3_out_5), .Q(R167_q));  // open: C, en
  Register #(.Bits(16)) R169 (.D(demultiplexer_3_out_7), .Q(R169_q));  // open: C, en
  Register #(.Bits(16)) R171 (.D(demultiplexer_3_out_9), .Q(R171_q));  // open: C, en
  Register #(.Bits(16)) RET_3 (.D(demultiplexer_3_out_11), .Q(RET_3_q));  // open: C, en
  Register #(.Bits(16)) Addr_3 (.D(demultiplexer_3_out_13), .Q(Addr_3_q));  // open: C, en
  CounterPreset #(.Bits(16)) PC_3 (
    .en(1'b1), .dir(1'b0), .in(demultiplexer_3_out_15), .out(PC_3_out));  // open: C, ld, clr, ovf
  Multiplexer #(.Bits(16)) multiplexer_15 (
    .sel(and_22_out[1]), .in_0(multiplexer_14_out), .in_1(add_3_s), .out(multiplexer_15_out));
  Multiplexer #(.Bits(16)) multiplexer_16 (
    .sel(and_22_out[2]), .in_0(multiplexer_14_out), .in_1(add_3_s), .out(multiplexer_16_out));
  Multiplexer #(.Bits(16)) multiplexer_17 (
    .sel(and_22_out[3]), .in_0(multiplexer_14_out), .in_1(add_3_s), .out(multiplexer_17_out));
  Multiplexer #(.Bits(16)) multiplexer_18 (
    .sel(and_22_out[4]), .in_0(multiplexer_14_out), .in_1(add_3_s), .out(multiplexer_18_out));
  Multiplexer #(.Bits(16)) multiplexer_19 (
    .sel(and_22_out[5]), .in_0(multiplexer_14_out), .in_1(add_3_s), .out(multiplexer_19_out));
  Multiplexer #(.Bits(16)) multiplexer_20 (
    .sel(and_22_out[6]), .in_0(multiplexer_14_out), .in_1(add_3_s), .out(multiplexer_20_out));
  Multiplexer #(.Bits(16)) multiplexer_21 (
    .sel(and_22_out[7]), .in_0(multiplexer_14_out), .in_1(add_3_s), .out(multiplexer_21_out));
  Multiplexer #(.Selector_Bits(4), .Bits(16)) multiplexer_22 (
    .in_0({16{1'b0}}), .in_1(R1_q), .in_2(R2_q), .in_3(R3_q), .in_4(R4_q), .in_5(R5_q), .in_6(R6_q),
    .in_7(R7_q), .in_8(R8_q), .in_9(R9_q), .in_10(BUF_2_q), .in_11(RET_2_q), .in_12(STA_2_q),
    .in_13(Addr_2_q), .in_14(Link_2_q), .in_15(PC_2_out), .out(multiplexer_22_out));  // open: sel
  Multiplexer #(.Selector_Bits(4), .Bits(16)) multiplexer_23 (
    .in_0({16{1'b0}}), .in_1(R1_q), .in_2(R2_q), .in_3(R3_q), .in_4(R4_q), .in_5(R5_q), .in_6(R6_q),
    .in_7(R7_q), .in_8(R8_q), .in_9(R9_q), .in_10(BUF_2_q), .in_11(RET_2_q), .in_12(STA_2_q),
    .in_13(Addr_2_q), .in_14(Link_2_q), .in_15(PC_2_out), .out(multiplexer_23_out));  // open: sel
  Multiplexer #(.Selector_Bits(4), .Bits(16)) multiplexer_24 (
    .in_0({16{1'b0}}), .in_1(R1_q), .in_2(R2_q), .in_3(R3_q), .in_4(R4_q), .in_5(R5_q), .in_6(R6_q),
    .in_7(R7_q), .in_8(R8_q), .in_9(R9_q), .in_10(BUF_2_q), .in_11(RET_2_q), .in_12(STA_2_q),
    .in_13(Addr_2_q), .in_14(Link_2_q), .in_15(PC_2_out), .out(multiplexer_24_out));  // open: sel
  Register #(.Bits(16)) R136 (.D(multiplexer_15_out), .C(CLK), .en(or_15_out[1]), .Q(R136_q));
  Register #(.Bits(16)) R137 (.D(multiplexer_16_out), .C(CLK), .en(or_15_out[2]), .Q(R137_q));
  Register #(.Bits(16)) R138 (.D(multiplexer_17_out), .C(CLK), .en(or_15_out[3]), .Q(R138_q));
  Register #(.Bits(16)) R139 (.D(multiplexer_18_out), .C(CLK), .en(or_15_out[4]), .Q(R139_q));
  Register #(.Bits(16)) R140 (.D(multiplexer_19_out), .C(CLK), .en(or_15_out[5]), .Q(R140_q));
  Register #(.Bits(16)) R141 (.D(multiplexer_20_out), .C(CLK), .en(or_15_out[6]), .Q(R141_q));
  Register #(.Bits(16)) R142 (.D(multiplexer_21_out), .C(CLK), .en(or_15_out[7]), .Q(R142_q));
  assign driver_1_out = decoder_3_out_7[0] ? {16{1'b0}} : 16'bz;  // Driver driver_1
  assign driver_1_out = decoder_3_out_7[1] ? R136_q : 16'bz;  // Driver driver_2
  assign driver_1_out = decoder_3_out_7[2] ? R137_q : 16'bz;  // Driver driver_3
  assign driver_1_out = decoder_3_out_7[3] ? R138_q : 16'bz;  // Driver driver_4
  assign driver_1_out = decoder_3_out_7[4] ? R139_q : 16'bz;  // Driver driver_5
  assign driver_1_out = decoder_3_out_7[5] ? R140_q : 16'bz;  // Driver driver_6
  assign driver_1_out = decoder_3_out_7[6] ? R141_q : 16'bz;  // Driver driver_7
  assign driver_1_out = decoder_3_out_7[7] ? R142_q : 16'bz;  // Driver driver_8
  assign driver_9_out = decoder_2_out_7[0] ? {16{1'b0}} : 16'bz;  // Driver driver_9
  assign driver_9_out = decoder_2_out_7[1] ? R136_q : 16'bz;  // Driver driver_10
  assign driver_9_out = decoder_2_out_7[2] ? R137_q : 16'bz;  // Driver driver_11
  assign driver_9_out = decoder_2_out_7[3] ? R138_q : 16'bz;  // Driver driver_12
  assign driver_9_out = decoder_2_out_7[4] ? R139_q : 16'bz;  // Driver driver_13
  assign driver_9_out = decoder_2_out_7[5] ? R140_q : 16'bz;  // Driver driver_14
  assign driver_9_out = decoder_2_out_7[6] ? R141_q : 16'bz;  // Driver driver_15
  assign driver_9_out = decoder_2_out_7[7] ? R142_q : 16'bz;  // Driver driver_16
  assign {driver_17_out_2, driver_17_out} = decoder_1_out_7[0] ? {16{1'b0}} : 16'bz;  // Driver driver_17
  // Probe on R136_q
  assign {driver_17_out_2, driver_17_out} = decoder_1_out_7[1] ? R136_q : 16'bz;  // Driver driver_18
  // Probe on R137_q
  assign {driver_17_out_2, driver_17_out} = decoder_1_out_7[2] ? R137_q : 16'bz;  // Driver driver_19
  // Probe on R138_q
  assign {driver_17_out_2, driver_17_out} = decoder_1_out_7[3] ? R138_q : 16'bz;  // Driver driver_20
  // Probe on R139_q
  assign {driver_17_out_2, driver_17_out} = decoder_1_out_7[4] ? R139_q : 16'bz;  // Driver driver_21
  // Probe on R140_q
  assign {driver_17_out_2, driver_17_out} = decoder_1_out_7[5] ? R140_q : 16'bz;  // Driver driver_22
  // Probe on R141_q
  assign {driver_17_out_2, driver_17_out} = decoder_1_out_7[6] ? R141_q : 16'bz;  // Driver driver_23
  // Probe on R142_q
  assign {driver_17_out_2, driver_17_out} = decoder_1_out_7[7] ? R142_q : 16'bz;  // Driver driver_24
  Multiplexer #(.Selector_Bits(4), .Bits(16)) multiplexer_25 (
    .in_1({16{1'b0}}), .in_2(R163_q), .in_3(R164_q), .in_4(R165_q), .in_5(R166_q), .in_6(R167_q),
    .in_7(R168_q), .in_8(R169_q), .in_9(R170_q), .in_10(R171_q), .in_11(BUF_3_q), .in_12(RET_3_q),
    .in_13(STA_3_q), .in_14(Addr_3_q), .in_15(Link_3_q));  // open: sel, in_0, out
  Multiplexer #(.Bits(16)) multiplexer_26 (
    .sel(and_22_out_2[0]), .in_0(multiplexer_14_out), .in_1(add_3_s), .out(multiplexer_26_out));
  Multiplexer #(.Bits(16)) multiplexer_27 (
    .sel(and_22_out_2[1]), .in_0(multiplexer_14_out), .in_1(add_3_s), .out(multiplexer_27_out));
  Multiplexer #(.Bits(16)) multiplexer_28 (
    .sel(and_22_out_2[2]), .in_0(multiplexer_14_out), .in_1(add_3_s), .out(multiplexer_28_out));
  Multiplexer #(.Bits(16)) multiplexer_29 (
    .sel(and_22_out_2[3]), .in_0(multiplexer_14_out), .in_1(add_3_s), .out(multiplexer_29_out));
  Multiplexer #(.Bits(16)) multiplexer_30 (
    .sel(and_22_out_2[4]), .in_0(multiplexer_14_out), .in_1(add_3_s), .out(multiplexer_30_out));
  Multiplexer #(.Bits(16)) multiplexer_31 (
    .sel(and_22_out_2[5]), .in_0(multiplexer_14_out), .in_1(add_3_s), .out(multiplexer_31_out));
  Multiplexer #(.Bits(16)) multiplexer_32 (
    .sel(and_22_out_2[6]), .in_0(multiplexer_14_out), .in_1(add_3_s), .out(multiplexer_32_out));
  Multiplexer #(.Bits(16)) multiplexer_33 (
    .sel(and_22_out_2[7]), .in_0(multiplexer_14_out), .in_1(add_3_s), .out(multiplexer_33_out));
  Register #(.Bits(16)) R143 (.D(multiplexer_26_out), .C(CLK), .en(or_15_out_2[0]), .Q(R143_q));
  Register #(.Bits(16)) R144 (.D(multiplexer_27_out), .C(CLK), .en(or_15_out_2[1]), .Q(R144_q));
  Register #(.Bits(16)) BUF_4 (.D(multiplexer_28_out), .C(CLK), .en(or_15_out_2[2]), .Q(BUF_4_q));
  Register #(.Bits(16)) RET_4 (.D(multiplexer_29_out), .C(CLK), .en(or_15_out_2[3]), .Q(RET_4_q));
  Register #(.Bits(16)) STA_4 (.D(multiplexer_30_out), .C(CLK), .en(or_15_out_2[4]), .Q(STA_4_q));
  Register #(.Bits(16)) Addr_4 (.D(multiplexer_31_out), .C(CLK), .en(or_15_out_2[5]), .Q(Addr_4_q));
  Register #(.Bits(16)) Link_4 (.D(multiplexer_32_out), .C(CLK), .en(or_15_out_2[6]), .Q(Link_4_q));
  CounterPreset #(.Bits(16)) PC_4 (
    .en(1'b1), .C(CLK), .dir(1'b0), .in(multiplexer_33_out), .ld(or_15_out_2[7]), .clr(1'b0), .out(PC_4_out));  // open: ovf
  Multiplexer #(.Selector_Bits(4), .Bits(16)) multiplexer_34 (
    .in_1({16{1'b0}}), .in_2(R163_q), .in_3(R164_q), .in_4(R165_q), .in_5(R166_q), .in_6(R167_q),
    .in_7(R168_q), .in_8(R169_q), .in_9(R170_q), .in_10(R171_q), .in_11(BUF_3_q), .in_12(RET_3_q),
    .in_13(STA_3_q), .in_14(Addr_3_q), .in_15(Link_3_q));  // open: sel, in_0, out
  assign driver_1_out = decoder_3_out_15[0] ? R143_q : 16'bz;  // Driver driver_25
  assign driver_1_out = decoder_3_out_15[1] ? R144_q : 16'bz;  // Driver driver_26
  assign driver_1_out = decoder_3_out_15[2] ? BUF_4_q : 16'bz;  // Driver driver_27
  assign driver_1_out = decoder_3_out_15[3] ? RET_4_q : 16'bz;  // Driver driver_28
  assign driver_1_out = decoder_3_out_15[4] ? STA_4_q : 16'bz;  // Driver driver_29
  assign driver_1_out = decoder_3_out_15[5] ? Addr_4_q : 16'bz;  // Driver driver_30
  assign driver_1_out = decoder_3_out_15[6] ? Link_4_q : 16'bz;  // Driver driver_31
  assign driver_1_out = decoder_3_out_15[7] ? PC_4_out : 16'bz;  // Driver driver_32
  assign driver_9_out = decoder_2_out_15[0] ? R143_q : 16'bz;  // Driver driver_33
  assign driver_9_out = decoder_2_out_15[1] ? R144_q : 16'bz;  // Driver driver_34
  assign driver_9_out = decoder_2_out_15[2] ? BUF_4_q : 16'bz;  // Driver driver_35
  assign driver_9_out = decoder_2_out_15[3] ? RET_4_q : 16'bz;  // Driver driver_36
  assign driver_9_out = decoder_2_out_15[4] ? STA_4_q : 16'bz;  // Driver driver_37
  assign driver_9_out = decoder_2_out_15[5] ? Addr_4_q : 16'bz;  // Driver driver_38
  assign driver_9_out = decoder_2_out_15[6] ? Link_4_q : 16'bz;  // Driver driver_39
  assign driver_9_out = decoder_2_out_15[7] ? PC_4_out : 16'bz;  // Driver driver_40
  assign {driver_17_out_2, driver_17_out} = decoder_1_out_15[0] ? R143_q : 16'bz;  // Driver driver_41
  assign {driver_17_out_2, driver_17_out} = decoder_1_out_15[1] ? R144_q : 16'bz;  // Driver driver_42
  assign {driver_17_out_2, driver_17_out} = decoder_1_out_15[2] ? BUF_4_q : 16'bz;  // Driver driver_43
  assign {driver_17_out_2, driver_17_out} = decoder_1_out_15[3] ? RET_4_q : 16'bz;  // Driver driver_44
  assign {driver_17_out_2, driver_17_out} = decoder_1_out_15[4] ? STA_4_q : 16'bz;  // Driver driver_45
  assign {driver_17_out_2, driver_17_out} = decoder_1_out_15[5] ? Addr_4_q : 16'bz;  // Driver driver_46
  assign {driver_17_out_2, driver_17_out} = decoder_1_out_15[6] ? Link_4_q : 16'bz;  // Driver driver_47
  assign {driver_17_out_2, driver_17_out} = decoder_1_out_15[7] ? PC_4_out : 16'bz;  // Driver driver_48
  // Probe on R143_q
  // Probe on R144_q
  // Probe on BUF_4_q
  // Probe on RET_4_q
  // Probe on STA_4_q
  // Probe on Addr_4_q
  // Probe on Link_4_q
  // Probe on PC_4_out
  Multiplexer #(.Selector_Bits(4), .Bits(16)) multiplexer_35 (
    .in_1({16{1'b0}}), .in_2(R163_q), .in_3(R164_q), .in_4(R165_q), .in_5(R166_q), .in_6(R167_q),
    .in_7(R168_q), .in_8(R169_q), .in_9(R170_q), .in_10(R171_q), .in_11(BUF_3_q), .in_12(RET_3_q),
    .in_13(STA_3_q), .in_14(Addr_3_q), .in_15(Link_3_q));  // open: sel, in_0, out
  Register Z_4 (.C(undriven_49), .en(undriven_51), .Q(Z_4_q));  // open: D
  Register N_4 (.C(undriven_49), .en(undriven_51), .Q(N_4_q));  // open: D
  Register C_4 (.C(undriven_49), .en(undriven_51), .Q(C_4_q));  // open: D
  Register V_4 (.C(undriven_49), .en(undriven_51), .Q(V_4_q));  // open: D
  Register Z_5 (.C(undriven_48), .en(undriven_50), .Q(Z_5_q));  // open: D
  Register N_5 (.C(undriven_48), .en(undriven_50), .Q(N_5_q));  // open: D
  Register C_5 (.C(undriven_48), .en(undriven_50), .Q(C_5_q));  // open: D
  Register V_5 (.C(undriven_48), .en(undriven_50), .Q(V_5_q));  // open: D
  Demultiplexer #(.Selector_Bits(4), .Bits(16)) demultiplexer_4 (
    .out_0(demultiplexer_4_out_0), .out_1(demultiplexer_4_out_1), .out_2(demultiplexer_4_out_2),
    .out_3(demultiplexer_4_out_3), .out_4(demultiplexer_4_out_4), .out_5(demultiplexer_4_out_5),
    .out_6(demultiplexer_4_out_6), .out_7(demultiplexer_4_out_7), .out_8(demultiplexer_4_out_8),
    .out_9(demultiplexer_4_out_9), .out_10(demultiplexer_4_out_10), .out_11(demultiplexer_4_out_11),
    .out_12(demultiplexer_4_out_12), .out_13(demultiplexer_4_out_13), .out_14(demultiplexer_4_out_14),
    .out_15(demultiplexer_4_out_15));  // open: sel, in
  Demultiplexer #(.Selector_Bits(4), .Bits(16)) demultiplexer_5 (
    .out_0(demultiplexer_5_out_0), .out_1(demultiplexer_5_out_1), .out_2(demultiplexer_5_out_2),
    .out_3(demultiplexer_5_out_3), .out_4(demultiplexer_5_out_4), .out_5(demultiplexer_5_out_5),
    .out_6(demultiplexer_5_out_6), .out_7(demultiplexer_5_out_7), .out_8(demultiplexer_5_out_8),
    .out_9(demultiplexer_5_out_9), .out_10(demultiplexer_5_out_10), .out_11(demultiplexer_5_out_11),
    .out_12(demultiplexer_5_out_12), .out_13(demultiplexer_5_out_13), .out_14(demultiplexer_5_out_14),
    .out_15(demultiplexer_5_out_15));  // open: sel, in
  Add #(.Bits(16)) add_7 (.a(multiplexer_44_out), .b(multiplexer_42_out), .c_i(C_4_q), .s(add_7_s), .c_o(add_7_c_o));
  Sub #(.Bits(16)) sub_4 (.a(multiplexer_44_out), .b(multiplexer_42_out), .c_i(C_4_q), .s(sub_4_s), .c_o(sub_4_c_o));
  Mul #(.Bits(16)) mul_4 (.a(multiplexer_44_out), .b(multiplexer_42_out), .mul({mul_4_mul_2, mul_4_mul}));
  Div #(.Bits(16)) div_4 (.a(multiplexer_44_out), .b(multiplexer_42_out), .q(div_4_q), .r(div_4_r));
  assign and_23_out = multiplexer_44_out & multiplexer_42_out;  // And and_23, 16 bits wide
  assign or_16_out = multiplexer_44_out | multiplexer_42_out;  // Or or_16, 16 bits wide
  assign xor_11_out = multiplexer_44_out ^ multiplexer_42_out;  // XOr xor_11, 16 bits wide
  assign nor_5_out = ~(multiplexer_44_out | multiplexer_42_out);  // NOr nor_5, 16 bits wide
  Add #(.Bits(16)) add_8 (.a(multiplexer_46_out), .b(multiplexer_45_out), .c_i(C_5_q), .s(add_8_s), .c_o(add_8_c_o));
  Sub #(.Bits(16)) sub_5 (.a(multiplexer_46_out), .b(multiplexer_45_out), .c_i(C_5_q), .s(sub_5_s), .c_o(sub_5_c_o));
  Mul #(.Bits(16)) mul_5 (.a(multiplexer_46_out), .b(multiplexer_45_out), .mul({mul_5_mul_2, mul_5_mul}));
  Div #(.Bits(16)) div_5 (.a(multiplexer_46_out), .b(multiplexer_45_out), .q(div_5_q), .r(div_5_r));
  assign and_24_out = multiplexer_46_out & multiplexer_45_out;  // And and_24, 16 bits wide
  assign or_17_out = multiplexer_46_out | multiplexer_45_out;  // Or or_17, 16 bits wide
  assign xor_12_out = multiplexer_46_out ^ multiplexer_45_out;  // XOr xor_12, 16 bits wide
  assign nor_6_out = ~(multiplexer_46_out | multiplexer_45_out);  // NOr nor_6, 16 bits wide
  Demultiplexer #(.Selector_Bits(4), .Bits(16)) demultiplexer_6 (
    .out_0(demultiplexer_6_out_0), .out_1(demultiplexer_6_out_1), .out_2(demultiplexer_6_out_2),
    .out_3(demultiplexer_6_out_3), .out_4(demultiplexer_6_out_4), .out_5(demultiplexer_6_out_5),
    .out_6(demultiplexer_6_out_6), .out_7(demultiplexer_6_out_7), .out_8(demultiplexer_6_out_8),
    .out_9(demultiplexer_6_out_9), .out_10(demultiplexer_6_out_10), .out_11(demultiplexer_6_out_11),
    .out_12(demultiplexer_6_out_12), .out_13(demultiplexer_6_out_13), .out_14(demultiplexer_6_out_14),
    .out_15(demultiplexer_6_out_15));  // open: sel, in
  Demultiplexer #(.Selector_Bits(4), .Bits(16)) demultiplexer_7 (
    .out_0({demultiplexer_7_out_0_2, demultiplexer_7_out_0[0]}), .out_1(demultiplexer_7_out_1),
    .out_2(demultiplexer_7_out_2), .out_3(demultiplexer_7_out_3),
    .out_4({demultiplexer_7_out_4, undriven_36[0]}), .out_5(demultiplexer_7_out_5),
    .out_6(demultiplexer_7_out_6), .out_7(demultiplexer_7_out_7),
    .out_8({demultiplexer_7_out_8, undriven_40[0]}), .out_9(demultiplexer_7_out_9),
    .out_10(demultiplexer_7_out_10), .out_11(demultiplexer_7_out_11),
    .out_12({demultiplexer_7_out_12, undriven_44[0]}), .out_13(demultiplexer_7_out_13),
    .out_14(demultiplexer_7_out_14), .out_15(demultiplexer_7_out_15));  // open: sel, in
  Register #(.Bits(16)) R110 (.D(demultiplexer_4_out_2), .Q(R110_q));  // open: C, en
  Register #(.Bits(16)) R112 (.D(demultiplexer_4_out_4), .Q(R112_q));  // open: C, en
  Register #(.Bits(16)) R114 (.D(demultiplexer_4_out_6), .Q(R114_q));  // open: C, en
  Register #(.Bits(16)) R116 (.D(demultiplexer_4_out_8), .Q(R116_q));  // open: C, en
  Register #(.Bits(16)) BUF_5 (.D(demultiplexer_4_out_10), .Q(BUF_5_q));  // open: C, en
  Register #(.Bits(16)) STA_5 (.D(demultiplexer_4_out_12), .Q(STA_5_q));  // open: C, en
  Register #(.Bits(16)) Link_5 (.D(demultiplexer_4_out_14), .Q(Link_5_q));  // open: C, en
  Register #(.Bits(16)) R109 (.D(demultiplexer_4_out_1), .Q(R109_q));  // open: C, en
  Register #(.Bits(16)) R111 (.D(demultiplexer_4_out_3), .Q(R111_q));  // open: C, en
  Register #(.Bits(16)) R113 (.D(demultiplexer_4_out_5), .Q(R113_q));  // open: C, en
  Register #(.Bits(16)) R115 (.D(demultiplexer_4_out_7), .Q(R115_q));  // open: C, en
  Register #(.Bits(16)) R117 (.D(demultiplexer_4_out_9), .Q(R117_q));  // open: C, en
  Register #(.Bits(16)) RET_5 (.D(demultiplexer_4_out_11), .Q(RET_5_q));  // open: C, en
  Register #(.Bits(16)) Addr_5 (.D(demultiplexer_4_out_13), .Q(Addr_5_q));  // open: C, en
  CounterPreset #(.Bits(16)) PC_5 (
    .en(1'b1), .dir(1'b0), .in(demultiplexer_4_out_15), .out(PC_5_out));  // open: C, ld, clr, ovf
  Register #(.Bits(16)) R119 (.D(demultiplexer_5_out_2), .Q(R119_q));  // open: C, en
  Register #(.Bits(16)) R121 (.D(demultiplexer_5_out_4), .Q(R121_q));  // open: C, en
  Register #(.Bits(16)) R123 (.D(demultiplexer_5_out_6), .Q(R123_q));  // open: C, en
  Register #(.Bits(16)) R125 (.D(demultiplexer_5_out_8), .Q(R125_q));  // open: C, en
  Register #(.Bits(16)) BUF_6 (.D(demultiplexer_5_out_10), .Q(BUF_6_q));  // open: C, en
  Register #(.Bits(16)) STA_6 (.D(demultiplexer_5_out_12), .Q(STA_6_q));  // open: C, en
  Register #(.Bits(16)) Link_6 (.D(demultiplexer_5_out_14), .Q(Link_6_q));  // open: C, en
  Multiplexer #(.Selector_Bits(4), .Bits(16)) multiplexer_36 (
    .in_0(undriven_63), .in_1(undriven_62), .in_2(undriven_61), .in_3(undriven_60), .in_4(undriven_59),
    .in_5(undriven_58), .in_6(add_7_s), .in_7(sub_4_s), .in_8(mul_4_mul), .in_9(mul_4_mul_2),
    .in_10(div_4_q), .in_11(div_4_r), .in_12(and_23_out), .in_13(or_16_out), .in_14(xor_11_out),
    .in_15(nor_5_out), .out(multiplexer_36_out));  // open: sel
  Multiplexer #(.Selector_Bits(4), .Bits(16)) multiplexer_37 (
    .in_0(undriven_52), .in_1(undriven_53), .in_2(undriven_54), .in_3(undriven_55), .in_4(undriven_56),
    .in_5(undriven_57), .in_6(add_8_s), .in_7(sub_5_s), .in_8(mul_5_mul), .in_9(mul_5_mul_2),
    .in_10(div_5_q), .in_11(div_5_r), .in_12(and_24_out), .in_13(or_17_out), .in_14(xor_12_out),
    .in_15(nor_6_out), .out(multiplexer_37_out));  // open: sel
  Demultiplexer #(.Selector_Bits(4), .Bits(16)) demultiplexer_8 (
    .in(multiplexer_36_out), .out_0(demultiplexer_8_out_0), .out_1(demultiplexer_8_out_1),
    .out_2(demultiplexer_8_out_2), .out_3(demultiplexer_8_out_3), .out_4(demultiplexer_8_out_4),
    .out_5(demultiplexer_8_out_5), .out_6(demultiplexer_8_out_6), .out_7(demultiplexer_8_out_7),
    .out_8(demultiplexer_8_out_8), .out_9(demultiplexer_8_out_9), .out_10(demultiplexer_8_out_10),
    .out_11(demultiplexer_8_out_11), .out_12(demultiplexer_8_out_12), .out_13(demultiplexer_8_out_13),
    .out_14(demultiplexer_8_out_14), .out_15(demultiplexer_8_out_15));  // open: sel
  Demultiplexer #(.Selector_Bits(4), .Bits(16)) demultiplexer_9 (
    .in(multiplexer_37_out), .out_0(demultiplexer_9_out_0), .out_1(demultiplexer_9_out_1),
    .out_2(demultiplexer_9_out_2), .out_3(demultiplexer_9_out_3), .out_4(demultiplexer_9_out_4),
    .out_5(demultiplexer_9_out_5), .out_6(demultiplexer_9_out_6), .out_7(demultiplexer_9_out_7),
    .out_8(demultiplexer_9_out_8), .out_9(demultiplexer_9_out_9), .out_10(demultiplexer_9_out_10),
    .out_11(demultiplexer_9_out_11), .out_12(demultiplexer_9_out_12), .out_13(demultiplexer_9_out_13),
    .out_14(demultiplexer_9_out_14), .out_15(demultiplexer_9_out_15));  // open: sel
  Register #(.Bits(16)) t29 (.D(undriven_34), .Q(t29_q));  // open: C, en
  Register #(.Bits(16)) t30 (.D(undriven_36), .Q({t30_q, undriven_5[0]}));  // open: C, en
  Register #(.Bits(16)) t31 (.D(undriven_38), .Q(t31_q));  // open: C, en
  Register #(.Bits(16)) t32 (.D(undriven_40), .Q({t32_q, undriven_9[0]}));  // open: C, en
  Register #(.Bits(16)) t33 (.D(undriven_42), .Q(t33_q));  // open: C, en
  Register #(.Bits(16)) t34 (.D(undriven_44), .Q({t34_q, undriven_13[0]}));  // open: C, en
  Register #(.Bits(16)) t35 (.D(undriven_46), .Q(t35_q));  // open: C, en
  Register #(.Bits(16)) R118 (.D(demultiplexer_5_out_1), .Q(R118_q));  // open: C, en
  Register #(.Bits(16)) R120 (.D(demultiplexer_5_out_3), .Q(R120_q));  // open: C, en
  Register #(.Bits(16)) R122 (.D(demultiplexer_5_out_5), .Q(R122_q));  // open: C, en
  Register #(.Bits(16)) R124 (.D(demultiplexer_5_out_7), .Q(R124_q));  // open: C, en
  Register #(.Bits(16)) R126 (.D(demultiplexer_5_out_9), .Q(R126_q));  // open: C, en
  Register #(.Bits(16)) RET_6 (.D(demultiplexer_5_out_11), .Q(RET_6_q));  // open: C, en
  Register #(.Bits(16)) Addr_6 (.D(demultiplexer_5_out_13), .Q(Addr_6_q));  // open: C, en
  CounterPreset #(.Bits(16)) PC_6 (
    .en(1'b1), .dir(1'b0), .in(demultiplexer_5_out_15), .out(PC_6_out));  // open: C, ld, clr, ovf
  Register #(.Bits(16)) R128 (.D(demultiplexer_6_out_2), .Q(R128_q));  // open: C, en
  Register #(.Bits(16)) R130 (.D(demultiplexer_6_out_4), .Q(R130_q));  // open: C, en
  Register #(.Bits(16)) R132 (.D(demultiplexer_6_out_6), .Q(R132_q));  // open: C, en
  Register #(.Bits(16)) R134 (.D(demultiplexer_6_out_8), .Q(R134_q));  // open: C, en
  Register #(.Bits(16)) BUF_7 (.D(demultiplexer_6_out_10), .Q(BUF_7_q));  // open: C, en
  Register #(.Bits(16)) STA_7 (.D(demultiplexer_6_out_12), .Q(STA_7_q));  // open: C, en
  Register #(.Bits(16)) Link_7 (.D(demultiplexer_6_out_14), .Q(Link_7_q));  // open: C, en
  Register #(.Bits(16)) t36 (.D(undriven_33), .Q(t36_q));  // open: C, en
  Register #(.Bits(16)) t37 (.D(undriven_35), .Q(t37_q));  // open: C, en
  Register #(.Bits(16)) t38 (.D(undriven_37), .Q(t38_q));  // open: C, en
  Register #(.Bits(16)) t39 (.D(undriven_39), .Q(t39_q));  // open: C, en
  Register #(.Bits(16)) t40 (.D(undriven_41), .Q(t40_q));  // open: C, en
  Register #(.Bits(16)) t41 (.D(undriven_43), .Q(t41_q));  // open: C, en
  Register #(.Bits(16)) t42 (.D(undriven_45), .Q(t42_q));  // open: C, en
  CounterPreset #(.Bits(16)) PC_7 (
    .en(1'b1), .dir(1'b0), .in(undriven_47), .clr(1'b0), .out(PC_7_out));  // open: C, ld, ovf
  Register #(.Bits(16)) R127 (.D(demultiplexer_6_out_1), .Q(R127_q));  // open: C, en
  Register #(.Bits(16)) R129 (.D(demultiplexer_6_out_3), .Q(R129_q));  // open: C, en
  Register #(.Bits(16)) R131 (.D(demultiplexer_6_out_5), .Q(R131_q));  // open: C, en
  Register #(.Bits(16)) R133 (.D(demultiplexer_6_out_7), .Q(R133_q));  // open: C, en
  Register #(.Bits(16)) R135 (.D(demultiplexer_6_out_9), .Q(R135_q));  // open: C, en
  Register #(.Bits(16)) RET_7 (.D(demultiplexer_6_out_11), .Q(RET_7_q));  // open: C, en
  Register #(.Bits(16)) Addr_7 (.D(demultiplexer_6_out_13), .Q(Addr_7_q));  // open: C, en
  CounterPreset #(.Bits(16)) PC_8 (
    .en(1'b1), .dir(1'b0), .in(demultiplexer_6_out_15), .out(PC_8_out));  // open: C, ld, clr, ovf
  Register #(.Bits(16)) R146 (.D(demultiplexer_8_out_2), .C(undriven_49), .Q(R146_q));  // open: en
  Register #(.Bits(16)) R148 (.D(demultiplexer_8_out_4), .C(undriven_49), .Q(R148_q));  // open: en
  Register #(.Bits(16)) R150 (.D(demultiplexer_8_out_6), .C(undriven_49), .Q(R150_q));  // open: en
  Register #(.Bits(16)) R152 (.D(demultiplexer_8_out_8), .C(undriven_49), .Q(R152_q));  // open: en
  Register #(.Bits(16)) BUF_8 (.D(demultiplexer_8_out_10), .C(undriven_49), .Q(BUF_8_q));  // open: en
  Register #(.Bits(16)) STA_8 (.D(demultiplexer_8_out_12), .C(undriven_49), .Q(STA_8_q));  // open: en
  Register #(.Bits(16)) Link_8 (.D(demultiplexer_8_out_14), .C(undriven_49), .Q(Link_8_q));  // open: en
  Register #(.Bits(16)) R92 (.D(demultiplexer_9_out_2), .C(undriven_48), .Q(R92_q));  // open: en
  Register #(.Bits(16)) R94 (.D(demultiplexer_9_out_4), .C(undriven_48), .Q(R94_q));  // open: en
  Register #(.Bits(16)) R96 (.D(demultiplexer_9_out_6), .C(undriven_48), .Q(R96_q));  // open: en
  Register #(.Bits(16)) R98 (.D(demultiplexer_9_out_8), .C(undriven_48), .Q(R98_q));  // open: en
  Register #(.Bits(16)) BUF_9 (.D(demultiplexer_9_out_10), .C(undriven_48), .Q(BUF_9_q));  // open: en
  Register #(.Bits(16)) STA_9 (.D(demultiplexer_9_out_12), .C(undriven_48), .Q(STA_9_q));  // open: en
  Register #(.Bits(16)) Link_9 (.D(demultiplexer_9_out_14), .C(undriven_48), .Q(Link_9_q));  // open: en
  Register #(.Bits(16)) R145 (.D(demultiplexer_8_out_1), .C(undriven_49), .Q(R145_q));  // open: en
  Register #(.Bits(16)) R147 (.D(demultiplexer_8_out_3), .C(undriven_49), .Q(R147_q));  // open: en
  Register #(.Bits(16)) R149 (.D(demultiplexer_8_out_5), .C(undriven_49), .Q(R149_q));  // open: en
  Register #(.Bits(16)) R151 (.D(demultiplexer_8_out_7), .C(undriven_49), .Q(R151_q));  // open: en
  Register #(.Bits(16)) R153 (.D(demultiplexer_8_out_9), .C(undriven_49), .Q(R153_q));  // open: en
  Register #(.Bits(16)) RET_8 (.D(demultiplexer_8_out_11), .C(undriven_49), .Q(RET_8_q));  // open: en
  Register #(.Bits(16)) Addr_8 (.D(demultiplexer_8_out_13), .C(undriven_49), .Q(Addr_8_q));  // open: en
  CounterPreset #(.Bits(16)) PC_9 (
    .en(1'b1), .dir(1'b0), .in(demultiplexer_8_out_15), .clr(1'b0), .out(PC_9_out));  // open: C, ld, ovf
  Register #(.Bits(16)) R91 (.D(demultiplexer_9_out_1), .C(undriven_48), .Q(R91_q));  // open: en
  Register #(.Bits(16)) R93 (.D(demultiplexer_9_out_3), .C(undriven_48), .Q(R93_q));  // open: en
  Register #(.Bits(16)) R95 (.D(demultiplexer_9_out_5), .C(undriven_48), .Q(R95_q));  // open: en
  Register #(.Bits(16)) R97 (.D(demultiplexer_9_out_7), .C(undriven_48), .Q(R97_q));  // open: en
  Register #(.Bits(16)) R99 (.D(demultiplexer_9_out_9), .C(undriven_48), .Q(R99_q));  // open: en
  Register #(.Bits(16)) RET_9 (.D(demultiplexer_9_out_11), .C(undriven_48), .Q(RET_9_q));  // open: en
  Register #(.Bits(16)) Addr_9 (.D(demultiplexer_9_out_13), .C(undriven_48), .Q(Addr_9_q));  // open: en
  CounterPreset #(.Bits(16)) PC_10 (
    .en(1'b1), .dir(1'b0), .in(demultiplexer_9_out_15), .clr(1'b0), .out(PC_10_out));  // open: C, ld, ovf
  Multiplexer #(.Selector_Bits(4), .Bits(16)) multiplexer_38 (
    .in_1({16{1'b0}}), .in_2(R109_q), .in_3(R110_q), .in_4(R111_q), .in_5(R112_q), .in_6(R113_q),
    .in_7(R114_q), .in_8(R115_q), .in_9(R116_q), .in_10(R117_q), .in_11(BUF_5_q), .in_12(RET_5_q),
    .in_13(STA_5_q), .in_14(Addr_5_q), .in_15(Link_5_q));  // open: sel, in_0, out
  Multiplexer #(.Selector_Bits(4), .Bits(16)) multiplexer_39 (
    .in_0(undriven), .in_1(undriven_2), .in_2(undriven_3), .in_3(undriven_4), .in_4(undriven_5),
    .in_5(undriven_6), .in_6(undriven_7), .in_7(undriven_8), .in_8(undriven_9), .in_9(undriven_10),
    .in_10(undriven_11), .in_11(undriven_12), .in_12(undriven_13), .in_13(undriven_14), .in_14(undriven_15),
    .in_15(undriven_16), .out(multiplexer_39_out));  // open: sel
  Multiplexer #(.Selector_Bits(4), .Bits(16)) multiplexer_40 (
    .in_0({undriven_17, undriven[0]}), .in_1({undriven_18, undriven_2[0]}),
    .in_2({undriven_19, undriven_3[0]}), .in_3({undriven_20, undriven_4[0]}),
    .in_4({undriven_21, undriven_5[0]}), .in_5({undriven_22, undriven_6[0]}),
    .in_6({undriven_23, undriven_7[0]}), .in_7({undriven_24, undriven_8[0]}),
    .in_8({undriven_25, undriven_9[0]}), .in_9({undriven_26, undriven_10[0]}),
    .in_10({undriven_27, undriven_11[0]}), .in_11({undriven_28, undriven_12[0]}),
    .in_12({undriven_29, undriven_13[0]}), .in_13({undriven_30, undriven_14[0]}),
    .in_14({undriven_31, undriven_15[0]}), .in_15({undriven_32, undriven_16[0]}), .out(multiplexer_40_out));  // open: sel
  Multiplexer #(.Selector_Bits(4), .Bits(16)) multiplexer_41 (
    .in_0({16{1'b0}}), .in_1(R127_q), .in_2(R128_q), .in_3(R129_q), .in_4(R130_q), .in_5(R131_q),
    .in_6(R132_q), .in_7(R133_q), .in_8(R134_q), .in_9(R135_q), .in_10(BUF_7_q), .in_11(RET_7_q),
    .in_12(STA_7_q), .in_13(Addr_7_q), .in_14(Link_7_q), .in_15(PC_8_out), .out(multiplexer_41_out));  // open: sel
  Multiplexer #(.Selector_Bits(4), .Bits(16)) multiplexer_42 (
    .in_0({16{1'b0}}), .in_1(R145_q), .in_2(R146_q), .in_3(R147_q), .in_4(R148_q), .in_5(R149_q),
    .in_6(R150_q), .in_7(R151_q), .in_8(R152_q), .in_9(R153_q), .in_10(BUF_8_q), .in_11(RET_8_q),
    .in_12(STA_8_q), .in_13(Addr_8_q), .in_14(Link_8_q), .in_15(PC_9_out), .out(multiplexer_42_out));  // open: sel
  Multiplexer #(.Selector_Bits(4), .Bits(16)) multiplexer_43 (
    .in_0({16{1'b0}}), .in_1(R145_q), .in_2(R146_q), .in_3(R147_q), .in_4(R148_q), .in_5(R149_q),
    .in_6(R150_q), .in_7(R151_q), .in_8(R152_q), .in_9(R153_q), .in_10(BUF_8_q), .in_11(RET_8_q),
    .in_12(STA_8_q), .in_13(Addr_8_q), .in_14(Link_8_q), .in_15(PC_9_out), .out(multiplexer_43_out));  // open: sel
  Multiplexer #(.Selector_Bits(4), .Bits(16)) multiplexer_44 (
    .in_0({16{1'b0}}), .in_1(R145_q), .in_2(R146_q), .in_3(R147_q), .in_4(R148_q), .in_5(R149_q),
    .in_6(R150_q), .in_7(R151_q), .in_8(R152_q), .in_9(R153_q), .in_10(BUF_8_q), .in_11(RET_8_q),
    .in_12(STA_8_q), .in_13(Addr_8_q), .in_14(Link_8_q), .in_15(PC_9_out), .out(multiplexer_44_out));  // open: sel
  Multiplexer #(.Selector_Bits(4), .Bits(16)) multiplexer_45 (
    .in_0({16{1'b0}}), .in_1(R91_q), .in_2(R92_q), .in_3(R93_q), .in_4(R94_q), .in_5(R95_q), .in_6(R96_q),
    .in_7(R97_q), .in_8(R98_q), .in_9(R99_q), .in_10(BUF_9_q), .in_11(RET_9_q), .in_12(STA_9_q),
    .in_13(Addr_9_q), .in_14(Link_9_q), .in_15(PC_10_out), .out(multiplexer_45_out));  // open: sel
  Multiplexer #(.Selector_Bits(4), .Bits(16)) multiplexer_46 (
    .in_0({16{1'b0}}), .in_1(R91_q), .in_2(R92_q), .in_3(R93_q), .in_4(R94_q), .in_5(R95_q), .in_6(R96_q),
    .in_7(R97_q), .in_8(R98_q), .in_9(R99_q), .in_10(BUF_9_q), .in_11(RET_9_q), .in_12(STA_9_q),
    .in_13(Addr_9_q), .in_14(Link_9_q), .in_15(PC_10_out), .out(multiplexer_46_out));  // open: sel
  Multiplexer #(.Selector_Bits(4), .Bits(16)) multiplexer_47 (
    .in_1({16{1'b0}}), .in_2(R109_q), .in_3(R110_q), .in_4(R111_q), .in_5(R112_q), .in_6(R113_q),
    .in_7(R114_q), .in_8(R115_q), .in_9(R116_q), .in_10(R117_q), .in_11(BUF_5_q), .in_12(RET_5_q),
    .in_13(STA_5_q), .in_14(Addr_5_q), .in_15(Link_5_q));  // open: sel, in_0, out
  Multiplexer #(.Selector_Bits(4), .Bits(16)) multiplexer_48 (
    .in_0({16{1'b0}}), .in_1(R118_q), .in_2(R119_q), .in_3(R120_q), .in_4(R121_q), .in_5(R122_q),
    .in_6(R123_q), .in_7(R124_q), .in_8(R125_q), .in_9(R126_q), .in_10(BUF_6_q), .in_11(RET_6_q),
    .in_12(STA_6_q), .in_13(Addr_6_q), .in_14(Link_6_q), .in_15(PC_6_out), .out(multiplexer_48_out));  // open: sel
  Multiplexer #(.Selector_Bits(4), .Bits(16)) multiplexer_49 (
    .in_0({16{1'b0}}), .in_1(R118_q), .in_2(R119_q), .in_3(R120_q), .in_4(R121_q), .in_5(R122_q),
    .in_6(R123_q), .in_7(R124_q), .in_8(R125_q), .in_9(R126_q), .in_10(BUF_6_q), .in_11(RET_6_q),
    .in_12(STA_6_q), .in_13(Addr_6_q), .in_14(Link_6_q), .in_15(PC_6_out), .out(multiplexer_49_out));  // open: sel
  Multiplexer #(.Selector_Bits(4), .Bits(16)) multiplexer_50 (
    .in_0({16{1'b0}}), .in_1(R127_q), .in_2(R128_q), .in_3(R129_q), .in_4(R130_q), .in_5(R131_q),
    .in_6(R132_q), .in_7(R133_q), .in_8(R134_q), .in_9(R135_q), .in_10(BUF_7_q), .in_11(RET_7_q),
    .in_12(STA_7_q), .in_13(Addr_7_q), .in_14(Link_7_q), .in_15(PC_8_out), .out(multiplexer_50_out));  // open: sel
  Multiplexer #(.Selector_Bits(4), .Bits(16)) multiplexer_51 (
    .in_1({16{1'b0}}), .in_2(R109_q), .in_3(R110_q), .in_4(R111_q), .in_5(R112_q), .in_6(R113_q),
    .in_7(R114_q), .in_8(R115_q), .in_9(R116_q), .in_10(R117_q), .in_11(BUF_5_q), .in_12(RET_5_q),
    .in_13(STA_5_q), .in_14(Addr_5_q), .in_15(Link_5_q));  // open: sel, in_0, out
  // Pins of 16 and 17 bits meet at undriven_78
  // Pins of 16 and 17 bits meet at {undriven_77[16], demultiplexer_2_out_1}
  // Pins of 16 and 17 bits meet at {undriven_76[16], demultiplexer_2_out_2}
  // Pins of 16 and 17 bits meet at {undriven_75[16], demultiplexer_2_out_3}
  // Pins of 16 and 17 bits meet at {undriven_74[16], demultiplexer_2_out_4}
  // Pins of 16 and 17 bits meet at {undriven_73[16], demultiplexer_2_out_5}
  // Pins of 16 and 17 bits meet at {undriven_72[16], demultiplexer_2_out_6}
  // Pins of 16 and 17 bits meet at {undriven_71[16], demultiplexer_2_out_7}
  // Pins of 16 and 17 bits meet at {undriven_70[16], demultiplexer_2_out_8}
  // Pins of 16 and 17 bits meet at {undriven_69[16], demultiplexer_2_out_9}
  // Pins of 16 and 17 bits meet at {undriven_68[16], demultiplexer_2_out_10}
  // Pins of 16 and 17 bits meet at {undriven_67[16], demultiplexer_2_out_11}

  // Notes on the sheet:
  //   CLK: Hz: 10
  //   CLK_2: Hz: 10
  //   INSTR loads fibbo.asm.hex
  //   contents of MEM (hex, n*v repeats v):
  //   b520
  //   CONTROL UNIT
  //   OPERAND
  //   OPCODE
  //   INSTR_2 loads fibbo.asm.hex
  //   contents of MEM_2 (hex, n*v repeats v):
  //   b520
  //   NOR
  //   XOR
  //   CLK
  //   Rm
  //   Rn
  //   Rd
  //   IMM8
  //   OPRAND
  //   LDR
  //   MemWE
  //   RnWE
  //   NZCV EN
  //   CV SEL
  //   NZCV ON
  //   NZCV RST
  //   FLAG ON
  //   FLAG RESET
  //   CONDITIONS
  //   N
  //   Z
  //   C
  //   V
  //   NS
  //   NC
  //   ZS
  //   ZC
  //   CS
  //   CC
  //   VS
  //   VC
  //   SM
  //   HI
  //   LT
  //   GT
  //   LE
  //   GE
  //   FC
  //   AL
  //   OP
  //   CND
  //   Dd
  //   Dn
  //   PC
  //   BRANCH
  //   POST IDX
  //   CMOVE
  //   MVS
  //   SHIFT
  //   DnIN
  //   Dm
  //   INSERT
  //   MOV
  //   CNS
  //   SFT
  //   CARRY
  //   NZCV CONTROL UNIT
  //   DdIN
  //   ALU
  //   NZCV SELECT BIT
  //   NZCV REGISTERS
  //   REGISTER FILE
  //   STR
  //   ADD
  //   SUB
  //   MUL
  //   LML
  //   DIV
  //   MOD
  //   AND
  //   ORR
  //   WE
  //   Didx
  //   Zero
  //   Buffer Register
  //   Return Register
  //   Stack Pointer
  //   Address Register
  //   Link Register
  //   Program Counter
endmodule
